// Logisim project macrothingy.circ as structural Verilog: 3 circuits, main circuit Incr1bit
module Incr1bit (
  input  A,
  input  in_2,
  output S,
  output Cout
);

  wire and_2_out, and_3_out, not_1_out, not_2_out;

  not not_1 (not_1_out, A);
  not not_2 (not_2_out, in_2);
  and and_1 (Cout, A, in_2);
  and and_2 (and_2_out, not_1_out, in_2);
  and and_3 (and_3_out, A, not_2_out);
  or or_1 (S, and_2_out, and_3_out);
endmodule

module splitterthingy (
  input  [7:0] in_1,
  output [7:0] out_2
);

  wire incr1bit1_1_out_3, incr1bit_1_cout, incr1bit_2_cout, incr1bit_3_cout, incr1bit_4_cout,
       incr1bit_5_cout, incr1bit_6_cout;

  incr1bit1 incr1bit1_1 (.A(in_1[0]), .out_2(out_2[0]), .out_3(incr1bit1_1_out_3));
  Incr1bit incr1bit_1 (.A(in_1[1]), .S(out_2[1]), .Cout(incr1bit_1_cout), .in_2(incr1bit1_1_out_3));
  Incr1bit incr1bit_2 (.A(in_1[2]), .S(out_2[2]), .Cout(incr1bit_2_cout), .in_2(incr1bit_1_cout));
  Incr1bit incr1bit_3 (.A(in_1[3]), .S(out_2[3]), .Cout(incr1bit_3_cout), .in_2(incr1bit_2_cout));
  Incr1bit incr1bit_4 (.A(in_1[4]), .S(out_2[4]), .Cout(incr1bit_4_cout), .in_2(incr1bit_3_cout));
  Incr1bit incr1bit_5 (.A(in_1[5]), .S(out_2[5]), .Cout(incr1bit_5_cout), .in_2(incr1bit_4_cout));
  Incr1bit incr1bit_6 (.A(in_1[6]), .S(out_2[6]), .Cout(incr1bit_6_cout), .in_2(incr1bit_5_cout));
  Incr1bit incr1bit_7 (.A(in_1[7]), .S(out_2[7]), .in_2(incr1bit_6_cout));  // open: Cout
endmodule

module incr1bit1 (
  input  A,
  output out_2,
  output out_3
);

  not not_1 (out_2, A);

  assign out_3 = A;
endmodule
