// Logisim project play.circ as structural Verilog: 1 circuit, main circuit main
module main (
  input  A,
  input  B,
  input  in_3,
  input  C,
  input  A_2,
  input  in_6,
  input  B_2,
  input  A3,
  input  B3,
  input  C3,
  output X,
  output Y,
  output W,
  output X_2,
  output Y_2,
  output out_16,
  output Z,
  output out_18
);

  wire _000_out, _00_out, _001_out, _01_out, and_1_out, or_1_out, xor_1_out;

  or or_1 (or_1_out, B, C);
  and and_1 (and_1_out, A, B);
  not not_1 (Y, or_1_out);
  not not_2 (X, xor_1_out);
  xor xor_1 (xor_1_out, and_1_out, Y);
  and _000 (_000_out, ~A3, ~B3, ~C3);  // AND_Gate
  and _001 (_001_out, ~B3, ~C3);  // AND_Gate
  // AND_Gate _010 is placed but not wired
  // AND_Gate _100 is placed but not wired
  // AND_Gate _110 is placed but not wired
  // AND_Gate _111 is placed but not wired
  and _00 (_00_out, ~A_2, ~B_2);  // AND_Gate
  and _01 (_01_out, ~A_2, B_2);  // AND_Gate
  or or_2 (out_18, _000_out, _001_out);
  or or_3 (out_16, _00_out, _01_out);
  and and_2 (W, ~in_3, ~in_6);  // AND_Gate
  // XOR_Gate xor_2 is placed but not wired
endmodule
